// Logisim project 2.Mux8_1.circ as structural Verilog
module main (
  input  in_1,
  input  in_2,
  input  in_3,
  input  in_4,
  input  in_5,
  input  in_6,
  input  in_7,
  input  in_8,
  input  in_9,
  input  in_10,
  input  in_11,
  output out_12
);

  mux8_1 mux8_1_1 (
    .a(in_1), .b(in_2), .c(in_3), .d(in_4), .e(in_5), .f(in_6), .g(in_7), .h(in_8),
    .ch({in_9, in_10, in_11}), .data(out_12));
endmodule

// VHDL entity mux8_1, as the project stores it:
--library and package
library ieee;
use ieee.std_logic_1164.all;
use ieee.std_logic_arith.all;
use ieee.std_logic_unsigned.all;

--entity
entity mux8_1 is
    port(
        a, b, c, d, e, f, g, h : in  std_logic;                     -- 입력 8개
        ch                     : in  std_logic_vector(2 downto 0);  -- 채널 선택 1개
        data                   : out std_logic                      -- 출력 1개
    );
end entity mux8_1;

--architecture
architecture bhv of mux8_1 is
begin
    process(a, b, c, d, e, f, g, h, ch)
    begin
        case ch is
            when "000" => data <= a;
            when "001" => data <= b;
            when "010" => data <= c;
            when "011" => data <= d;
            when "100" => data <= e;
            when "101" => data <= f;
            when "110" => data <= g;
            when "111" => data <= h;
            when others => data <= '0';
        end case;
    end process;
end architecture bhv;
