// Logisim project 3.Digital_tube.circ as structural Verilog: 1 circuit, main circuit main
module main (
  input  g,
  input  f,
  input  a,
  input  b,
  input  e,
  input  d,
  input  c,
  input  dp
);

  _7_Segment_Display u_7_segment_display_1 (.g(g), .f(f), .a(a), .b(b), .e(e), .d(d), .c(c), .dp(dp));
endmodule
