// Logisim project 5.count_number_led.circ as structural Verilog
module main (
  input  in_1
);

  wire a, b, c, d, dp, e, f, g;
  wire [12:0] dipswitch_1_sw1;

  DipSwitch #(.number(13)) dipswitch_1 (
    .sw1(dipswitch_1_sw1[0]), .sw2(dipswitch_1_sw1[1]), .sw3(dipswitch_1_sw1[2]), .sw4(dipswitch_1_sw1[3]),
    .sw5(dipswitch_1_sw1[4]), .sw6(dipswitch_1_sw1[5]), .sw7(dipswitch_1_sw1[7]), .sw8(dipswitch_1_sw1[6]),
    .sw9(dipswitch_1_sw1[8]), .sw10(dipswitch_1_sw1[9]), .sw11(dipswitch_1_sw1[10]),
    .sw12(dipswitch_1_sw1[11]), .sw13(dipswitch_1_sw1[12]));
  _7_Segment_Display u_7_segment_display_1 (.g(g), .f(f), .a(a), .b(b), .e(e), .d(d), .c(c), .dp(dp));
  count_led count_led_1 (.en(in_1), .vt(dipswitch_1_sw1), .display({a, b, c, d, e, f, g, dp}));
endmodule

// VHDL entity count_led, as the project stores it:
--library and package
library ieee;
use ieee.std_logic_1164.all;
use ieee.std_logic_arith.all;
use ieee.std_logic_unsigned.all;

--entity
entity count_led is
    port(
        en      : in  std_logic;                       -- enable
        vt      : in  std_logic_vector(13 downto 1);   -- 13비트 입력
        display : out std_logic_vector(7 downto 0)     -- a b c d e f g dp
    );
end entity count_led;

--architecture
architecture bhv of count_led is
begin
    process(en, vt)
        variable sum : integer range 0 to 13;
    begin
        -- 1. '1'의 개수 세기
        sum := 0;
        for i in 1 to 13 loop
            if vt(i) = '1' then
                sum := sum + 1;
            end if;
        end loop;

        -- 2. enable 판단 후 표시
        if en = '0' then
            display <= "00000000";                       -- 꺼짐
        else
            case sum is
                when 0  => display <= "11111100";        -- 0
                when 1  => display <= "01100000";        -- 1
                when 2  => display <= "11011010";        -- 2
                when 3  => display <= "11110010";        -- 3
                when 4  => display <= "01100110";        -- 4
                when 5  => display <= "10110110";        -- 5
                when 6  => display <= "10111110";        -- 6
                when 7  => display <= "11100000";        -- 7
                when 8  => display <= "11111110";        -- 8
                when 9  => display <= "11100110";        -- 9
                when 10 => display <= "11101110";        -- A
                when 11 => display <= "00111110";        -- b
                when 12 => display <= "10011100";        -- C
                when 13 => display <= "01111010";        -- d
                when others => display <= "00000000";
            end case;
        end if;
    end process;
end architecture bhv;
