// Logisim project 1.RS_Latch.circ as structural Verilog
module main (
  input  S,
  input  R,
  input  in_3,
  input  in_4,
  output not_Q,
  output Q,
  output out_7,
  output out_8
);

  nor nor_1 (not_Q, S, Q);
  nor nor_2 (Q, not_Q, R);
  rs_latch rs_latch_1 (.S(in_3), .R(in_4), .Qn(out_7), .Q(out_8));
endmodule

// VHDL entity rs_latch, as the project stores it:
library ieee;
use ieee.std_logic_1164.all;

entity rs_latch is
    port (
        S  : in  std_logic;
        R  : in  std_logic;
        Qn : out std_logic;
        Q  : out std_logic
    );
end rs_latch;

architecture gate_level of rs_latch is
    signal q_int  : std_logic;
    signal qn_int : std_logic;
begin
    -- upper NOR gate : S, Q  -> Qn
    qn_int <= S nor q_int;

    -- lower NOR gate : R, Qn -> Q
    q_int  <= R nor qn_int;

    Qn <= qn_int;
    Q  <= q_int;
end gate_level;
