// Logisim project 2.D_Latch.circ as structural Verilog
module main (
  input  D,
  input  En,
  input  in_3,
  input  in_4,
  output Q,
  output Not_Q,
  output out_7,
  output out_8
);

  wire nand_1_out, nand_2_out;

  nand nand_1 (nand_1_out, D, En);
  nand nand_2 (nand_2_out, nand_1_out, En);
  nand nand_3 (Q, nand_1_out, Not_Q);
  nand nand_4 (Not_Q, Q, nand_2_out);
  d_latch d_latch_1 (.D(in_3), .en(in_4), .Q(out_7), .Qn(out_8));
endmodule

// VHDL entity d_latch, as the project stores it:
-- ============================================================
-- Exercise 2 : D Latch (with Enable, level-sensitive)
--   en = '1' : Q follows D (transparent)
--   en = '0' : keep previous state (Hold)
-- ============================================================
library ieee;
use ieee.std_logic_1164.all;

entity d_latch is
    port (
        D  : in  std_logic;
        en : in  std_logic;
        Q  : out std_logic;
        Qn : out std_logic
    );
end d_latch;

architecture behavioral of d_latch is
    signal q_int : std_logic := '0';
begin
    process (D, en)
    begin
        if en = '1' then
            q_int <= D;
        end if;          -- en = '0' : no assignment -> Hold
    end process;

    Q  <= q_int;
    Qn <= not q_int;
end behavioral;
