// Logisim project 3.D_Filp_Flop.circ as structural Verilog
module main (
  input  D,
  input  Clk,
  input  in_3,
  input  in_4,
  output Q,
  output NQ,
  output out_7,
  output out_8
);

  wire nand_1_out, nand_2_out, nand_3_out, nand_4_out, nand_5_out, nand_6_out, not_1_out, not_2_out,
       not_3_out, not_4_out;

  not not_1 (not_1_out, Clk);
  not not_2 (not_2_out, D);
  nand nand_1 (nand_1_out, D, not_1_out);
  nand nand_2 (nand_2_out, not_1_out, not_2_out);
  d_ff2 d_ff2_1 (.D(in_3), .clk(in_4), .Q(out_7), .Qn(out_8));
  nand nand_3 (nand_3_out, nand_1_out, nand_4_out);
  nand nand_4 (nand_4_out, nand_3_out, nand_2_out);
  not not_3 (not_3_out, not_1_out);
  not not_4 (not_4_out, nand_3_out);
  nand nand_5 (nand_5_out, nand_3_out, not_3_out);
  nand nand_6 (nand_6_out, not_3_out, not_4_out);
  nand nand_7 (Q, nand_5_out, NQ);
  nand nand_8 (NQ, Q, nand_6_out);
endmodule

// VHDL entity d_ff2, as the project stores it:
library ieee;
use ieee.std_logic_1164.all;

entity d_ff2 is
    port (
        D   : in  std_logic;
        clk : in  std_logic;
        Q   : out std_logic;
        Qn  : out std_logic
    );
end d_ff2;

architecture behavioral of d_ff2 is
    signal q_int : std_logic := '0';
begin
    process (clk)
    begin
        if rising_edge(clk) then
            q_int <= D;
        end if;
    end process;

    Q  <= q_int;
    Qn <= not q_int;
end behavioral;
