// Logisim project 4.JK_Flip_Flop.circ as structural Verilog
module main (
  input  J,
  input  CLK,
  input  K,
  input  CLRn,
  input  in_5,
  input  in_6,
  input  in_7,
  input  in_8,
  output Q,
  output NQ,
  output out_11,
  output out_12
);

  wire nand_1_out, nand_2_out, nand_3_out, nand_4_out, nand_5_out, nand_6_out, not_1_out;

  not not_1 (not_1_out, CLK);
  nand nand_1 (nand_1_out, NQ, J, not_1_out);
  nand nand_2 (nand_2_out, not_1_out, K, Q);
  nand nand_3 (nand_3_out, nand_1_out, nand_4_out);
  nand nand_4 (nand_4_out, nand_3_out, CLRn, nand_2_out);
  jk_ff jk_ff_1 (.J(in_5), .clk(in_6), .K(in_7), .CLRn(in_8), .Q(out_11), .Qn(out_12));
  nand nand_5 (nand_5_out, nand_3_out, CLK);
  nand nand_6 (nand_6_out, CLK, nand_4_out);
  nand nand_7 (Q, nand_5_out, NQ);
  nand nand_8 (NQ, Q, nand_6_out, CLRn);
endmodule

// VHDL entity jk_ff, as the project stores it:
library ieee;
use ieee.std_logic_1164.all;

entity jk_ff is
    port (
        J    : in  std_logic;
        clk  : in  std_logic;
        K    : in  std_logic;
        CLRn : in  std_logic;
        Q    : out std_logic;
        Qn   : out std_logic
    );
end jk_ff;

architecture behavioral of jk_ff is
    signal q_int : std_logic := '0';
    signal jk    : std_logic_vector(1 downto 0);
begin
    jk <= J & K;

    -- CLRn is active-low and asynchronous (same as the gate circuit)
    process (clk, CLRn)
    begin
        if CLRn = '0' then
            q_int <= '0';                             -- Clear
        elsif rising_edge(clk) then
            case jk is
                when "00"   => q_int <= q_int;        -- Hold
                when "01"   => q_int <= '0';          -- Reset
                when "10"   => q_int <= '1';          -- Set
                when "11"   => q_int <= not q_int;    -- Toggle
                when others => q_int <= q_int;
            end case;
        end if;
    end process;

    Q  <= q_int;
    Qn <= not q_int;
end behavioral;
